// Digital circuit hw2_circuit_equations.dig as structural Verilog
module hw2_circuit_equations (
  input  I,
  input  Clck,
  output X
);

  wire and_1_out, and_2_out, not_1_out, S0_q, S1_q;

  and and_1 (and_1_out, not_1_out, S0_q);
  and and_2 (and_2_out, S1_q, S0_q, I);
  not not_1 (not_1_out, S1_q);
  D_FF S1 (.D(and_1_out), .C(Clck), .Q(S1_q));  // open: nQ
  D_FF S0 (.D(and_2_out), .C(Clck), .Q(S0_q));  // open: nQ
  or or_1 (X, not_1_out, S0_q);
endmodule
